# Fritzing sketch 005-ruler (saved by Fritzing 0.9.10b)
breadboards: 1

parts:
  Part2 = Arduino Uno (Rev3)
  R1 = Resistor [tolerance=±5% resistance=2.2k package="0402 [SMD]"]
  HC-SR04_Sensor_1 = HC-SR04 Ultrasonic Distance Sensor

nets:
  N1: Part2.A0, R1.Pin_1, HC-SR04_Sensor_1.TRIG
  5V: Part2.5V, HC-SR04_Sensor_1.VCC
  GND: Part2.GND, HC-SR04_Sensor_1.GND
  N2: R1.Pin_0, HC-SR04_Sensor_1.ECHO
